// Logisim project 4BITCOMBINATIONALMULTIPLIER.circ as structural Verilog: 1 circuit, main circuit main
module main (
);

  wire and_3_out, and_5_out, and_6_out, and_7_out, and_9_out, and_11_out, and_12_out, and_13_out, and_15_out,
       and_17_out, and_18_out, and_19_out, and_21_out, and_23_out, and_24_out, and_25_out, and_26_out,
       and_27_out, and_28_out, and_29_out, and_30_out, and_31_out, and_32_out, and_33_out, and_34_out,
       and_35_out, and_36_out, and_37_out, and_38_out, and_39_out, and_40_out, and_41_out, and_42_out,
       and_43_out, and_44_out, binary_to_bcd_converter_1_p2, binary_to_bcd_converter_1_p3,
       binary_to_bcd_converter_1_p4, dipswitch_1_p1, dipswitch_1_p2, dipswitch_1_p3, dipswitch_2_p1,
       dipswitch_2_p2, dipswitch_2_p3, dipswitch_2_p4, dipswitch_2_p5, or_1_out, or_2_out, or_4_out,
       or_5_out, or_6_out, or_7_out, or_8_out, xor_2_out, xor_3_out, xor_4_out, xor_5_out, xor_6_out,
       xor_7_out, xor_8_out, xor_10_out, xor_11_out, xor_13_out, xor_14_out, xor_15_out, xor_16_out,
       xor_17_out;
  wire [7:0] and_1_out;

  // DipSwitch #(.number(4)) dipswitch_1: pin names not known; wires that end beside it: dipswitch_1_p1, dipswitch_1_p2, dipswitch_1_p3
  // DipSwitch #(.number(4)) dipswitch_2: pin names not known; wires that end beside it: dipswitch_2_p1, dipswitch_2_p2, dipswitch_2_p3, dipswitch_2_p4, dipswitch_2_p5
  and and_1 (and_1_out[0], dipswitch_1_p1, dipswitch_2_p2);
  and and_2 (and_1_out[0], dipswitch_1_p1, dipswitch_2_p2);
  and and_3 (and_3_out, dipswitch_1_p2, dipswitch_2_p2);
  and and_4 (and_3_out, dipswitch_1_p2, dipswitch_2_p2);
  and and_5 (and_5_out, dipswitch_1_p3, dipswitch_2_p2);
  and and_6 (and_6_out, dipswitch_2_p1, dipswitch_2_p2);
  and and_7 (and_7_out, dipswitch_2_p3, dipswitch_1_p1);
  and and_8 (and_7_out, dipswitch_2_p3, dipswitch_1_p1);
  and and_9 (and_9_out, dipswitch_2_p3, dipswitch_1_p2);
  and and_10 (and_9_out, dipswitch_2_p3, dipswitch_1_p2);
  and and_11 (and_11_out, dipswitch_2_p3, dipswitch_1_p3);
  and and_12 (and_12_out, dipswitch_2_p3, dipswitch_2_p1);
  and and_13 (and_13_out, dipswitch_2_p4, dipswitch_1_p1);
  and and_14 (and_13_out, dipswitch_2_p4, dipswitch_1_p1);
  and and_15 (and_15_out, dipswitch_2_p4, dipswitch_1_p2);
  and and_16 (and_15_out, dipswitch_2_p4, dipswitch_1_p2);
  and and_17 (and_17_out, dipswitch_2_p4, dipswitch_1_p3);
  and and_18 (and_18_out, dipswitch_2_p4, dipswitch_2_p1);
  and and_19 (and_19_out, dipswitch_2_p5, dipswitch_1_p1);
  and and_20 (and_19_out, dipswitch_2_p5, dipswitch_1_p1);
  and and_21 (and_21_out, dipswitch_2_p5, dipswitch_1_p2);
  and and_22 (and_21_out, dipswitch_2_p5, dipswitch_1_p2);
  and and_23 (and_23_out, dipswitch_2_p5, dipswitch_1_p3);
  and and_24 (and_24_out, dipswitch_2_p5, dipswitch_2_p1);
  and and_25 (and_25_out, and_3_out, and_7_out);
  xor xor_1 (and_1_out[1], and_3_out, and_7_out);
  xor xor_2 (xor_2_out, and_5_out, and_9_out);
  and and_26 (and_26_out, and_5_out, and_9_out);
  xor xor_3 (xor_3_out, and_11_out, and_6_out);
  and and_27 (and_27_out, and_11_out, and_6_out);
  xor xor_4 (xor_4_out, and_12_out, or_2_out);
  and and_28 (and_28_out, and_12_out, or_2_out);
  xor xor_5 (xor_5_out, and_24_out, or_5_out);
  and and_29 (and_29_out, and_25_out, xor_2_out);
  and and_30 (and_30_out, or_1_out, xor_3_out);
  and and_31 (and_31_out, and_24_out, or_5_out);
  xor xor_6 (xor_6_out, and_25_out, xor_2_out);
  xor xor_7 (xor_7_out, or_1_out, xor_3_out);
  xor xor_8 (xor_8_out, xor_4_out, and_17_out);
  and and_32 (and_32_out, xor_4_out, and_17_out);
  xor xor_9 (and_1_out[6], or_8_out, xor_5_out);
  and and_33 (and_33_out, or_8_out, xor_5_out);
  or or_1 (or_1_out, and_26_out, and_29_out);
  or or_2 (or_2_out, and_27_out, and_30_out);
  xor xor_10 (xor_10_out, and_28_out, and_18_out);
  and and_34 (and_34_out, and_28_out, and_18_out);
  or or_3 (and_1_out[7], and_31_out, and_33_out);
  xor xor_11 (xor_11_out, or_6_out, xor_8_out);
  and and_35 (and_35_out, or_6_out, xor_8_out);
  and and_36 (and_36_out, or_4_out, xor_10_out);
  xor xor_12 (and_1_out[2], xor_6_out, and_13_out);
  and and_37 (and_37_out, xor_6_out, and_13_out);
  xor xor_13 (xor_13_out, xor_7_out, and_15_out);
  and and_38 (and_38_out, xor_7_out, and_15_out);
  or or_4 (or_4_out, and_32_out, and_35_out);
  xor xor_14 (xor_14_out, or_4_out, xor_10_out);
  or or_5 (or_5_out, and_34_out, and_36_out);
  xor xor_15 (xor_15_out, and_37_out, xor_13_out);
  and and_39 (and_39_out, and_37_out, xor_13_out);
  xor xor_16 (xor_16_out, xor_11_out, and_21_out);
  xor xor_17 (xor_17_out, xor_14_out, and_23_out);
  or or_6 (or_6_out, and_38_out, and_39_out);
  and and_40 (and_40_out, xor_11_out, and_21_out);
  and and_41 (and_41_out, xor_14_out, and_23_out);
  xor xor_18 (and_1_out[4], and_44_out, xor_16_out);
  and and_42 (and_42_out, and_44_out, xor_16_out);
  xor xor_19 (and_1_out[5], or_7_out, xor_17_out);
  and and_43 (and_43_out, or_7_out, xor_17_out);
  xor xor_20 (and_1_out[3], xor_15_out, and_19_out);
  and and_44 (and_44_out, xor_15_out, and_19_out);
  or or_7 (or_7_out, and_40_out, and_42_out);
  or or_8 (or_8_out, and_41_out, and_43_out);
  // Binary_to_BCD_converter #(.binvalue(8)) binary_to_bcd_converter_1: pin names not known; wires that end beside it: and_1_out, binary_to_bcd_converter_1_p2, binary_to_bcd_converter_1_p3, binary_to_bcd_converter_1_p4
  _7_Segment_Display u_7_segment_display_1 ();  // open: g, f, a, b, e, d, c, dp
  // BCD_to_7_Segment_decoder bcd_to_7_segment_decoder_1: pin names not known; wires that end beside it: binary_to_bcd_converter_1_p2
  _7_Segment_Display u_7_segment_display_2 ();  // open: g, f, a, b, e, d, c, dp
  // BCD_to_7_Segment_decoder bcd_to_7_segment_decoder_2: pin names not known; wires that end beside it: binary_to_bcd_converter_1_p3
  _7_Segment_Display u_7_segment_display_3 ();  // open: g, f, a, b, e, d, c, dp
  // BCD_to_7_Segment_decoder bcd_to_7_segment_decoder_3: pin names not known; wires that end beside it: binary_to_bcd_converter_1_p4

  // Notes on the sheet:
  //   A
  //   B
endmodule
