// Logisim project 6BITBINARYTOBCD.circ as structural Verilog: 2 circuits, main circuit BINTOBCD
module BINTOBCD (
  input  A,
  input  B,
  input  C,
  input  D,
  input  E,
  input  F,
  output [3:0] Tens,
  output [3:0] Ones
);

  wire add3block_1_s0, add3block_1_s1, add3block_1_s2, add3block_2_s0, add3block_2_s1, add3block_2_s2;

  ADD3BLOCK add3block_1 (
    .A(1'b0), .B(A), .C(B), .D(C), .S3(Tens[2]), .S2(add3block_1_s2), .S1(add3block_1_s1), .S0(add3block_1_s0));
  ADD3BLOCK add3block_2 (
    .A(add3block_1_s2), .B(add3block_1_s1), .C(add3block_1_s0), .D(D), .S3(Tens[1]), .S2(add3block_2_s2),
    .S1(add3block_2_s1), .S0(add3block_2_s0));
  ADD3BLOCK add3block_3 (
    .A(add3block_2_s2), .B(add3block_2_s1), .C(add3block_2_s0), .D(E), .S3(Tens[0]), .S2(Ones[3]),
    .S1(Ones[2]), .S0(Ones[1]));

  assign Ones[0] = F;
  assign Tens[3] = 1'b0;
endmodule

module ADD3BLOCK (
  input  A,
  input  B,
  input  C,
  input  D,
  output S3,
  output S2,
  output S1,
  output S0
);

  wire and_1_out, and_2_out, and_3_out, and_4_out, and_5_out, and_6_out, and_7_out, and_8_out, and_9_out,
       and_10_out, and_11_out, and_12_out, and_13_out, and_14_out, and_15_out, and_16_out, and_17_out,
       and_18_out, and_19_out, and_20_out, and_21_out, and_22_out, and_23_out, and_24_out, not_1_out,
       not_2_out, not_3_out, not_4_out, or_1_out, or_3_out, or_5_out, or_6_out, or_8_out, or_9_out;

  not not_1 (not_1_out, A);
  not not_2 (not_2_out, B);
  not not_3 (not_3_out, C);
  not not_4 (not_4_out, D);
  and and_1 (and_1_out, B, D);
  and and_2 (and_2_out, B, C);
  and and_3 (and_3_out, B, not_3_out);
  and and_4 (and_4_out, A, not_2_out);
  and and_5 (and_5_out, not_3_out, D);
  and and_6 (and_6_out, A, C);
  and and_7 (and_7_out, A, B);
  and and_8 (and_8_out, not_1_out, not_2_out);
  and and_9 (and_9_out, A, not_2_out);
  and and_10 (and_10_out, not_3_out, not_4_out);
  and and_11 (and_11_out, A, B);
  and and_12 (and_12_out, not_1_out, not_2_out);
  and and_13 (and_13_out, B, C);
  or or_1 (or_1_out, and_1_out, and_2_out);
  and and_14 (and_14_out, and_3_out, not_4_out);
  and and_15 (and_15_out, and_4_out, and_5_out);
  and and_16 (and_16_out, and_6_out, not_4_out);
  and and_17 (and_17_out, and_7_out, C);
  and and_18 (and_18_out, and_8_out, C);
  and and_19 (and_19_out, C, D);
  and and_20 (and_20_out, and_9_out, and_10_out);
  and and_21 (and_21_out, and_11_out, D);
  and and_22 (and_22_out, and_12_out, D);
  and and_23 (and_23_out, and_13_out, not_4_out);
  or or_2 (S3, or_1_out, A);
  or or_3 (or_3_out, and_14_out, and_15_out);
  or or_4 (S2, or_3_out, or_5_out);
  or or_5 (or_5_out, and_16_out, and_17_out);
  or or_6 (or_6_out, and_18_out, and_19_out);
  or or_7 (S1, or_6_out, or_8_out);
  or or_8 (or_8_out, and_20_out, and_21_out);
  or or_9 (or_9_out, and_22_out, and_23_out);
  or or_10 (S0, or_9_out, and_24_out);
  and and_24 (and_24_out, A, not_4_out);
endmodule
