// Logisim project COMBINATIONALDIVIDER.circ as structural Verilog: 1 circuit, main circuit main
module main (
);

  wire and_1_out, and_2_out, and_3_out, and_4_out, and_5_out, and_6_out, and_7_out, and_8_out, and_9_out,
       and_10_out, and_11_out, and_12_out, and_13_out, and_14_out, and_15_out, and_16_out, and_17_out,
       and_18_out, and_19_out, and_20_out, and_21_out, and_22_out, and_23_out, and_24_out, and_25_out,
       and_26_out, and_27_out, and_28_out, and_29_out, and_30_out, and_31_out, and_32_out, and_33_out,
       and_34_out, and_35_out, and_36_out, and_37_out, and_38_out, and_39_out, and_40_out, and_41_out,
       and_42_out, and_43_out, and_44_out, and_45_out, and_46_out, and_47_out, and_48_out, and_49_out,
       and_50_out, and_51_out, and_52_out, and_53_out, and_54_out, and_55_out, and_56_out,
       binary_to_bcd_converter_1_p2, binary_to_bcd_converter_1_p3, binary_to_bcd_converter_2_p2,
       binary_to_bcd_converter_2_p3, dipswitch_1_p1, dipswitch_1_p2, dipswitch_1_p3, dipswitch_2_p1,
       dipswitch_2_p2, dipswitch_2_p3, dipswitch_2_p4, not_1_out, not_2_out, not_3_out, not_4_out, not_5_out,
       not_6_out, not_7_out, not_8_out, not_9_out, not_10_out, not_11_out, not_12_out, not_13_out,
       not_14_out, not_15_out, not_16_out, not_17_out, not_18_out, not_19_out, not_20_out, not_21_out,
       not_22_out, not_23_out, not_24_out, not_25_out, not_26_out, not_27_out, not_28_out, or_6_out,
       or_9_out, or_10_out, or_11_out, or_13_out, or_14_out, or_15_out, or_16_out, or_17_out, or_19_out,
       or_20_out, or_21_out, or_22_out, or_23_out, or_24_out, or_25_out, or_26_out, or_28_out, xor_1_out,
       xor_2_out, xor_3_out, xor_4_out, xor_5_out, xor_6_out, xor_7_out, xor_8_out, xor_9_out, xor_10_out,
       xor_11_out, xor_12_out, xor_13_out, xor_14_out, xor_15_out, xor_16_out, xor_17_out, xor_18_out,
       xor_19_out, xor_20_out, xor_21_out, xor_22_out, xor_23_out, xor_24_out, xor_25_out, xor_26_out,
       xor_27_out, xor_28_out;
  wire [3:0] or_2_out, or_27_out;

  // DipSwitch #(.number(4)) dipswitch_1: pin names not known; wires that end beside it: dipswitch_1_p1, dipswitch_1_p2, dipswitch_1_p3
  // DipSwitch #(.number(3)) dipswitch_2: pin names not known; wires that end beside it: dipswitch_2_p1, dipswitch_2_p2, dipswitch_2_p3, dipswitch_2_p4
  not not_1 (not_1_out, 1'b0);
  not not_2 (not_2_out, 1'b0);
  xor xor_1 (xor_1_out, or_10_out, not_1_out);
  and and_1 (and_1_out, or_10_out, not_1_out);
  not not_3 (not_3_out, or_2_out[0]);
  not not_4 (not_4_out, dipswitch_2_p4);
  xor xor_2 (xor_2_out, xor_1_out, or_11_out);
  and and_2 (and_2_out, xor_1_out, or_11_out);
  and and_3 (and_3_out, or_10_out, not_3_out);
  and and_4 (and_4_out, or_2_out[0], xor_2_out);
  not not_5 (not_5_out, dipswitch_2_p4);
  xor xor_3 (xor_3_out, or_6_out, not_2_out);
  and and_5 (and_5_out, or_6_out, not_2_out);
  not not_6 (not_6_out, or_2_out[1]);
  LED led_1 (.in(or_2_out[0]));
  or or_1 (or_27_out[3], and_3_out, and_4_out);
  xor xor_4 (xor_4_out, or_13_out, not_4_out);
  and and_6 (and_6_out, or_13_out, not_4_out);
  not not_7 (not_7_out, or_2_out[2]);
  and and_7 (and_7_out, xor_3_out, or_9_out);
  and and_8 (and_8_out, or_6_out, not_6_out);
  and and_9 (and_9_out, or_2_out[1], xor_6_out);
  or or_2 (or_2_out[0], and_1_out, and_2_out);
  LED led_2 (.in(or_27_out[3]));
  xor xor_5 (xor_5_out, 1'b0, not_5_out);
  and and_10 (and_10_out, 1'b0, not_5_out);
  not not_8 (not_8_out, or_2_out[3]);
  and and_11 (and_11_out, or_13_out, not_7_out);
  and and_12 (and_12_out, or_2_out[2], xor_7_out);
  xor xor_6 (xor_6_out, xor_3_out, or_9_out);
  and and_13 (and_13_out, xor_5_out, or_16_out);
  and and_14 (and_14_out, 1'b0, not_8_out);
  and and_15 (and_15_out, or_2_out[3], xor_8_out);
  xor xor_7 (xor_7_out, xor_4_out, or_14_out);
  and and_16 (and_16_out, xor_4_out, or_14_out);
  LED led_3 (.in(or_2_out[1]));
  or or_3 (or_2_out[1], and_5_out, and_7_out);
  // OR_Gate or_4 has open pins: in0=and_8_out, in1=and_9_out, out=open
  LED led_4 (.in(or_2_out[3]));
  xor xor_8 (xor_8_out, xor_5_out, or_16_out);
  LED led_5 (.in(or_2_out[2]));
  or or_5 (or_2_out[2], and_6_out, and_16_out);
  or or_6 (or_6_out, and_11_out, and_12_out);
  or or_7 (or_2_out[3], and_10_out, and_13_out);
  // OR_Gate or_8 has open pins: in0=and_14_out, in1=and_15_out, out=open
  not not_9 (not_9_out, dipswitch_2_p4);
  not not_10 (not_10_out, dipswitch_2_p4);
  xor xor_9 (xor_9_out, or_15_out, not_9_out);
  and and_17 (and_17_out, or_15_out, not_9_out);
  not not_11 (not_11_out, or_2_out[1]);
  xor xor_10 (xor_10_out, or_20_out, not_10_out);
  and and_18 (and_18_out, or_20_out, not_10_out);
  not not_12 (not_12_out, or_2_out[0]);
  not not_13 (not_13_out, dipswitch_2_p3);
  and and_19 (and_19_out, xor_9_out, or_19_out);
  and and_20 (and_20_out, or_15_out, not_11_out);
  and and_21 (and_21_out, or_2_out[1], xor_11_out);
  and and_22 (and_22_out, xor_10_out, or_17_out);
  and and_23 (and_23_out, or_20_out, not_12_out);
  and and_24 (and_24_out, or_2_out[0], xor_12_out);
  not not_14 (not_14_out, dipswitch_2_p3);
  xor xor_11 (xor_11_out, xor_9_out, or_19_out);
  xor xor_12 (xor_12_out, xor_10_out, or_17_out);
  xor xor_13 (xor_13_out, or_22_out, not_13_out);
  and and_25 (and_25_out, or_22_out, not_13_out);
  not not_15 (not_15_out, or_2_out[2]);
  or or_9 (or_9_out, and_17_out, and_19_out);
  or or_10 (or_10_out, and_20_out, and_21_out);
  or or_11 (or_11_out, and_18_out, and_22_out);
  or or_12 (or_27_out[2], and_23_out, and_24_out);
  LED led_6 (.in(or_27_out[2]));
  xor xor_14 (xor_14_out, 1'b0, not_14_out);
  and and_26 (and_26_out, 1'b0, not_14_out);
  not not_16 (not_16_out, or_2_out[3]);
  and and_27 (and_27_out, xor_13_out, or_23_out);
  and and_28 (and_28_out, or_22_out, not_15_out);
  and and_29 (and_29_out, or_2_out[2], xor_16_out);
  xor xor_15 (xor_15_out, xor_14_out, or_21_out);
  and and_30 (and_30_out, xor_14_out, or_21_out);
  and and_31 (and_31_out, 1'b0, not_16_out);
  and and_32 (and_32_out, or_2_out[3], xor_15_out);
  xor xor_16 (xor_16_out, xor_13_out, or_23_out);
  or or_13 (or_13_out, and_31_out, and_32_out);
  or or_14 (or_14_out, and_25_out, and_27_out);
  or or_15 (or_15_out, and_28_out, and_29_out);
  not not_17 (not_17_out, dipswitch_2_p3);
  or or_16 (or_16_out, and_26_out, and_30_out);
  not not_18 (not_18_out, dipswitch_2_p3);
  and and_33 (and_33_out, or_25_out, not_17_out);
  not not_19 (not_19_out, or_2_out[0]);
  xor xor_17 (xor_17_out, or_24_out, not_18_out);
  and and_34 (and_34_out, or_24_out, not_18_out);
  not not_20 (not_20_out, or_2_out[1]);
  xor xor_18 (xor_18_out, or_25_out, not_17_out);
  not not_21 (not_21_out, dipswitch_2_p2);
  not not_22 (not_22_out, dipswitch_2_p2);
  and and_35 (and_35_out, xor_17_out, or_28_out);
  and and_36 (and_36_out, or_24_out, not_20_out);
  and and_37 (and_37_out, or_2_out[1], xor_20_out);
  xor xor_19 (xor_19_out, xor_18_out, or_26_out);
  and and_38 (and_38_out, xor_18_out, or_26_out);
  and and_39 (and_39_out, or_25_out, not_19_out);
  and and_40 (and_40_out, or_2_out[0], xor_19_out);
  xor xor_20 (xor_20_out, xor_17_out, or_28_out);
  or or_17 (or_17_out, and_33_out, and_38_out);
  or or_18 (or_27_out[1], and_39_out, and_40_out);
  xor xor_21 (xor_21_out, dipswitch_2_p1, not_21_out);
  and and_41 (and_41_out, dipswitch_2_p1, not_21_out);
  not not_23 (not_23_out, or_2_out[3]);
  xor xor_22 (xor_22_out, dipswitch_1_p3, not_22_out);
  and and_42 (and_42_out, dipswitch_1_p3, not_22_out);
  not not_24 (not_24_out, or_2_out[2]);
  or or_19 (or_19_out, and_34_out, and_35_out);
  or or_20 (or_20_out, and_36_out, and_37_out);
  LED led_7 (.in(or_27_out[1]));
  and and_43 (and_43_out, xor_21_out, 1'b1);
  and and_44 (and_44_out, dipswitch_2_p1, not_23_out);
  and and_45 (and_45_out, or_2_out[3], xor_23_out);
  and and_46 (and_46_out, xor_22_out, 1'b1);
  and and_47 (and_47_out, dipswitch_1_p3, not_24_out);
  and and_48 (and_48_out, or_2_out[2], xor_24_out);
  xor xor_23 (xor_23_out, xor_21_out, 1'b1);
  xor xor_24 (xor_24_out, xor_22_out, 1'b1);
  or or_21 (or_21_out, and_41_out, and_43_out);
  or or_22 (or_22_out, and_44_out, and_45_out);
  or or_23 (or_23_out, and_42_out, and_46_out);
  or or_24 (or_24_out, and_47_out, and_48_out);
  not not_25 (not_25_out, dipswitch_2_p2);
  not not_26 (not_26_out, dipswitch_2_p2);
  not not_27 (not_27_out, or_2_out[1]);
  xor xor_25 (xor_25_out, dipswitch_1_p1, not_26_out);
  and and_49 (and_49_out, dipswitch_1_p1, not_26_out);
  not not_28 (not_28_out, or_2_out[0]);
  xor xor_26 (xor_26_out, dipswitch_1_p2, not_25_out);
  and and_50 (and_50_out, dipswitch_1_p2, not_25_out);
  and and_51 (and_51_out, xor_25_out, 1'b1);
  and and_52 (and_52_out, dipswitch_1_p1, not_28_out);
  and and_53 (and_53_out, or_2_out[0], xor_28_out);
  xor xor_27 (xor_27_out, xor_26_out, 1'b1);
  and and_54 (and_54_out, xor_26_out, 1'b1);
  and and_55 (and_55_out, dipswitch_1_p2, not_27_out);
  and and_56 (and_56_out, or_2_out[1], xor_27_out);
  xor xor_28 (xor_28_out, xor_25_out, 1'b1);
  or or_25 (or_25_out, and_55_out, and_56_out);
  or or_26 (or_26_out, and_49_out, and_51_out);
  or or_27 (or_27_out[0], and_52_out, and_53_out);
  LED led_8 (.in(or_27_out[0]));
  or or_28 (or_28_out, and_50_out, and_54_out);
  // Probe on or_27_out
  // Binary_to_BCD_converter #(.binvalue(4)) binary_to_bcd_converter_1: pin names not known; wires that end beside it: or_27_out, binary_to_bcd_converter_1_p2, binary_to_bcd_converter_1_p3
  // Binary_to_BCD_converter #(.binvalue(4)) binary_to_bcd_converter_2: pin names not known; wires that end beside it: or_2_out, binary_to_bcd_converter_2_p2, binary_to_bcd_converter_2_p3
  _7_Segment_Display u_7_segment_display_1 ();  // open: g, f, a, b, e, d, c, dp
  // BCD_to_7_Segment_decoder bcd_to_7_segment_decoder_1: pin names not known; wires that end beside it: binary_to_bcd_converter_2_p2
  _7_Segment_Display u_7_segment_display_2 ();  // open: g, f, a, b, e, d, c, dp
  // BCD_to_7_Segment_decoder bcd_to_7_segment_decoder_2: pin names not known; wires that end beside it: binary_to_bcd_converter_2_p3
  _7_Segment_Display u_7_segment_display_3 ();  // open: g, f, a, b, e, d, c, dp
  // BCD_to_7_Segment_decoder bcd_to_7_segment_decoder_3: pin names not known; wires that end beside it: binary_to_bcd_converter_1_p2
  _7_Segment_Display u_7_segment_display_4 ();  // open: g, f, a, b, e, d, c, dp
  // BCD_to_7_Segment_decoder bcd_to_7_segment_decoder_4: pin names not known; wires that end beside it: binary_to_bcd_converter_1_p3

  // Notes on the sheet:
  //   Q0
  //   R3
  //   Q1
  //   Q3
  //   Q2
  //   R2
  //   R1
  //   R0
  //   R:
endmodule
