// Logisim project COMBNATIONALMULTIPLIER.circ as structural Verilog: 1 circuit, main circuit main
module main (
);

  wire and_2_out, and_3_out, and_4_out, and_5_out, and_6_out, and_7_out, and_8_out, and_9_out, and_10_out,
       and_11_out, and_12_out, and_13_out, and_14_out, and_15_out, and_16_out, and_17_out, and_18_out,
       bcd_to_7_segment_decoder_1_p1, binary_to_bcd_converter_1_p3, dipswitch_1_p1, dipswitch_1_p2,
       dipswitch_2_p1, dipswitch_2_p2, dipswitch_2_p3, dipswitch_2_p4, or_1_out, or_3_out, xor_2_out,
       xor_3_out, xor_4_out, xor_5_out, xor_7_out;
  wire [5:0] and_1_out;

  // DipSwitch #(.number(3)) dipswitch_1: pin names not known; wires that end beside it: dipswitch_1_p1, dipswitch_1_p2
  // DipSwitch #(.number(3)) dipswitch_2: pin names not known; wires that end beside it: dipswitch_2_p1, dipswitch_2_p2, dipswitch_2_p3, dipswitch_2_p4
  and and_1 (and_1_out[0], dipswitch_1_p1, dipswitch_2_p1);
  and and_2 (and_2_out, dipswitch_1_p1, dipswitch_2_p2);
  and and_3 (and_3_out, dipswitch_1_p1, dipswitch_2_p3);
  and and_4 (and_4_out, dipswitch_1_p2, dipswitch_2_p1);
  and and_5 (and_5_out, dipswitch_1_p2, dipswitch_2_p2);
  and and_6 (and_6_out, dipswitch_1_p2, dipswitch_2_p3);
  and and_7 (and_7_out, dipswitch_2_p4, dipswitch_1_p2);
  and and_8 (and_8_out, dipswitch_2_p4, dipswitch_2_p2);
  and and_9 (and_9_out, dipswitch_2_p4, dipswitch_2_p3);
  and and_10 (and_10_out, and_5_out, and_7_out);
  xor xor_1 (and_1_out[1], and_2_out, and_4_out);
  and and_11 (and_11_out, and_2_out, and_4_out);
  xor xor_2 (xor_2_out, and_5_out, and_7_out);
  and and_12 (and_12_out, and_8_out, or_1_out);
  xor xor_3 (xor_3_out, and_12_out, and_9_out);
  and and_13 (and_13_out, and_12_out, and_9_out);
  and and_14 (and_14_out, xor_2_out, and_11_out);
  xor xor_4 (xor_4_out, and_8_out, or_1_out);
  xor xor_5 (xor_5_out, xor_2_out, and_11_out);
  xor xor_6 (and_1_out[4], xor_3_out, or_3_out);
  and and_15 (and_15_out, xor_3_out, or_3_out);
  or or_1 (or_1_out, and_14_out, and_10_out);
  xor xor_7 (xor_7_out, xor_4_out, and_6_out);
  and and_16 (and_16_out, xor_4_out, and_6_out);
  or or_2 (and_1_out[5], and_13_out, and_15_out);
  and and_17 (and_17_out, xor_7_out, and_18_out);
  and and_18 (and_18_out, and_3_out, xor_5_out);
  xor xor_8 (and_1_out[3], xor_7_out, and_18_out);
  xor xor_9 (and_1_out[2], xor_5_out, and_3_out);
  or or_3 (or_3_out, and_16_out, and_17_out);
  _7_Segment_Display u_7_segment_display_1 ();  // open: g, f, a, b, e, d, c, dp
  // BCD_to_7_Segment_decoder bcd_to_7_segment_decoder_1: pin names not known; wires that end beside it: bcd_to_7_segment_decoder_1_p1
  // Binary_to_BCD_converter #(.binvalue(6)) binary_to_bcd_converter_1: pin names not known; wires that end beside it: and_1_out, bcd_to_7_segment_decoder_1_p1, binary_to_bcd_converter_1_p3
  _7_Segment_Display u_7_segment_display_2 ();  // open: g, f, a, b, e, d, c, dp
  // BCD_to_7_Segment_decoder bcd_to_7_segment_decoder_2: pin names not known; wires that end beside it: binary_to_bcd_converter_1_p3

  // Notes on the sheet:
  //   A0B0
  //   A1B0
  //   A1B1
  //   A1B2
  //   A2B0
  //   A2B1
  //   A2B2
  //   A0B1
  //   A0B2
endmodule
