// Logisim project FULLADDERSUBTRACTOR.circ as structural Verilog: 1 circuit, main circuit main
module main (
  input  in_1
);

  wire and_1_out, and_2_out, and_3_out, and_4_out, and_5_out, and_6_out, and_7_out, and_8_out, and_9_out,
       and_10_out, and_11_out, and_12_out, and_13_out, and_14_out, and_15_out, and_16_out, and_17_out,
       and_18_out, and_20_out, and_21_out, and_22_out, binary_to_bcd_converter_1_p2,
       binary_to_bcd_converter_1_p3, dipswitch_1_p1, dipswitch_1_p2, dipswitch_1_p3, dipswitch_1_p4,
       dipswitch_2_p1, dipswitch_2_p2, dipswitch_2_p3, dipswitch_2_p4, not_1_out, not_2_out, not_3_out,
       not_4_out, not_5_out, not_6_out, or_1_out, or_2_out, or_3_out, or_4_out, xor_1_out, xor_2_out,
       xor_3_out, xor_4_out, xor_5_out, xor_6_out, xor_7_out, xor_8_out, xor_9_out, xor_10_out, xor_11_out,
       xor_12_out, xor_13_out, xor_14_out, xor_15_out, xor_16_out, xor_17_out, xor_18_out, xor_19_out,
       xor_20_out;
  wire [4:0] or_5_out;

  // DipSwitch #(.number(4)) dipswitch_1: pin names not known; wires that end beside it: dipswitch_1_p1, dipswitch_1_p2, dipswitch_1_p3, dipswitch_1_p4
  // DipSwitch #(.number(4)) dipswitch_2: pin names not known; wires that end beside it: dipswitch_2_p1, dipswitch_2_p2, dipswitch_2_p3, dipswitch_2_p4
  xor xor_1 (xor_1_out, dipswitch_2_p2, in_1);
  xor xor_2 (xor_2_out, dipswitch_2_p3, in_1);
  xor xor_3 (xor_3_out, dipswitch_2_p4, in_1);
  xor xor_4 (xor_4_out, dipswitch_2_p1, in_1);
  and and_1 (and_1_out, dipswitch_1_p2, xor_1_out);
  xor xor_5 (xor_5_out, dipswitch_1_p4, xor_3_out);
  and and_2 (and_2_out, dipswitch_1_p4, xor_3_out);
  xor xor_6 (xor_6_out, dipswitch_1_p1, xor_4_out);
  and and_3 (and_3_out, dipswitch_1_p1, xor_4_out);
  xor xor_7 (xor_7_out, dipswitch_1_p2, xor_1_out);
  xor xor_8 (xor_8_out, dipswitch_1_p3, xor_2_out);
  and and_4 (and_4_out, dipswitch_1_p3, xor_2_out);
  xor xor_9 (xor_9_out, or_3_out, xor_7_out);
  and and_5 (and_5_out, or_3_out, xor_7_out);
  and and_6 (and_6_out, or_1_out, xor_8_out);
  xor xor_10 (xor_10_out, or_4_out, xor_5_out);
  and and_7 (and_7_out, or_4_out, xor_5_out);
  xor xor_11 (xor_11_out, in_1, xor_6_out);
  and and_8 (and_8_out, in_1, xor_6_out);
  xor xor_12 (xor_12_out, or_1_out, xor_8_out);
  or or_1 (or_1_out, and_5_out, and_1_out);
  or or_2 (or_2_out, and_7_out, and_2_out);
  not not_1 (not_1_out, or_2_out);
  or or_3 (or_3_out, and_8_out, and_3_out);
  xor xor_13 (xor_13_out, xor_9_out, and_9_out);
  xor xor_14 (xor_14_out, xor_12_out, and_9_out);
  or or_4 (or_4_out, and_6_out, and_4_out);
  xor xor_15 (xor_15_out, xor_10_out, and_9_out);
  and and_9 (and_9_out, in_1, not_1_out);
  and and_10 (and_10_out, xor_13_out, in_1);
  and and_11 (and_11_out, in_1, xor_15_out);
  and and_12 (and_12_out, xor_13_out, not_2_out);
  not not_2 (not_2_out, in_1);
  and and_13 (and_13_out, in_1, xor_14_out);
  and and_14 (and_14_out, xor_15_out, not_3_out);
  not not_3 (not_3_out, in_1);
  xor xor_16 (xor_16_out, xor_11_out, and_9_out);
  and and_15 (and_15_out, xor_16_out, in_1);
  and and_16 (and_16_out, xor_14_out, not_4_out);
  not not_4 (not_4_out, in_1);
  and and_17 (and_17_out, 1'b1, and_9_out);
  and and_18 (and_18_out, xor_16_out, not_5_out);
  not not_5 (not_5_out, in_1);
  and and_19 (or_5_out[4], or_2_out, not_6_out);
  or or_5 (or_5_out[0], xor_17_out, and_18_out);
  or or_6 (or_5_out[1], xor_18_out, and_12_out);
  or or_7 (or_5_out[2], and_16_out, xor_19_out);
  not not_6 (not_6_out, in_1);
  // Probe on binary_to_bcd_converter_1_p2
  // Binary_to_BCD_converter #(.binvalue(5)) binary_to_bcd_converter_1: pin names not known; wires that end beside it: or_5_out, binary_to_bcd_converter_1_p2, binary_to_bcd_converter_1_p3
  _7_Segment_Display u_7_segment_display_1 (.g(and_9_out));  // open: f, a, b, e, d, c, dp
  or or_8 (or_5_out[3], xor_20_out, and_14_out);
  and and_20 (and_20_out, and_15_out, and_17_out);
  _7_Segment_Display u_7_segment_display_2 ();  // open: g, f, a, b, e, d, c, dp
  // BCD_to_7_Segment_decoder bcd_to_7_segment_decoder_1: pin names not known; wires that end beside it: binary_to_bcd_converter_1_p2
  xor xor_17 (xor_17_out, and_17_out, and_15_out);
  _7_Segment_Display u_7_segment_display_3 ();  // open: g, f, a, b, e, d, c, dp
  // BCD_to_7_Segment_decoder bcd_to_7_segment_decoder_2: pin names not known; wires that end beside it: binary_to_bcd_converter_1_p3
  and and_21 (and_21_out, and_10_out, and_20_out);
  // Probe on binary_to_bcd_converter_1_p3
  xor xor_18 (xor_18_out, and_10_out, and_20_out);
  xor xor_19 (xor_19_out, and_13_out, and_21_out);
  and and_22 (and_22_out, and_13_out, and_21_out);
  xor xor_20 (xor_20_out, and_11_out, and_22_out);

  // Notes on the sheet:
  //   A in
  //   B in
  //   MSB ^
  //   INCREMETER OF DOOM
  //   <-- LSB
endmodule
