// Logisim project FULLCALC.circ as structural Verilog: 1 circuit, main circuit main
module main (
  input  in_1
);

  wire addsub_1_negative, addsub_1_s0, addsub_1_s1, addsub_1_s2, addsub_1_s3, addsub_1_s4, and_1_out,
       and_2_out, combdiv_1_q0, combdiv_1_q1, combdiv_1_q2, combdiv_1_q3, combdiv_1_r0, combdiv_1_r1,
       combdiv_1_r2, combdiv_1_r3, dipswitch_1_p1, dipswitch_1_p2, dipswitch_1_p3, dipswitch_2_p1,
       dipswitch_2_p2, dipswitch_2_p3, dipswitch_3_p1, dipswitch_3_p2, dipswitch_3_p3, dipswitch_3_p4,
       dipswitch_4_p1, dipswitch_4_p2, dipswitch_4_p3, dipswitch_4_p4, dipswitch_5_p1, dipswitch_5_p2,
       dipswitch_5_p3, dipswitch_6_p1, dipswitch_6_p2, dipswitch_6_p3, dipswitch_6_p4, multiplexer_1_out,
       multiplexer_2_out, multiplexer_3_out, multiplexer_4_out, multiplexer_5_out, multiplexer_6_out,
       mutipl_1_s0, mutipl_1_s1, mutipl_1_s2, mutipl_1_s3, mutipl_1_s4, mutipl_1_s5;
  wire [1:0] dipswitch_7_sw2;
  wire [3:0] bintobcd_1_ones, bintobcd_1_tens;

  // DipSwitch #(.number(3)) dipswitch_1: pin names not known; wires that end beside it: dipswitch_1_p1, dipswitch_1_p2, dipswitch_1_p3
  // DipSwitch #(.number(3)) dipswitch_2: pin names not known; wires that end beside it: dipswitch_2_p1, dipswitch_2_p2, dipswitch_2_p3
  // DipSwitch #(.number(4)) dipswitch_3: pin names not known; wires that end beside it: dipswitch_3_p1, dipswitch_3_p2, dipswitch_3_p3, dipswitch_3_p4
  // DipSwitch #(.number(4)) dipswitch_4: pin names not known; wires that end beside it: dipswitch_4_p1, dipswitch_4_p2, dipswitch_4_p3, dipswitch_4_p4, dipswitch_4_p1
  // DipSwitch #(.number(4)) dipswitch_5: pin names not known; wires that end beside it: dipswitch_5_p1, dipswitch_5_p2, dipswitch_5_p3
  // DipSwitch #(.number(3)) dipswitch_6: pin names not known; wires that end beside it: dipswitch_6_p1, dipswitch_6_p2, dipswitch_6_p3, dipswitch_6_p4
  COMBDIV combdiv_1 (
    .A0(dipswitch_5_p1), .A1(dipswitch_5_p2), .A2(dipswitch_5_p3), .A3(dipswitch_6_p1), .B0(dipswitch_6_p2),
    .B1(dipswitch_6_p3), .B2(dipswitch_6_p4), .Q0(combdiv_1_q0), .Q1(combdiv_1_q1), .Q2(combdiv_1_q2),
    .Q3(combdiv_1_q3), .R0(combdiv_1_r0), .R1(combdiv_1_r1), .R2(combdiv_1_r2), .R3(combdiv_1_r3));
  MUTIPL mutipl_1 (
    .A0(dipswitch_1_p1), .A1(dipswitch_1_p2), .A2(dipswitch_1_p3), .B0(dipswitch_2_p1), .B1(dipswitch_2_p2),
    .B2(dipswitch_2_p3), .S0(mutipl_1_s0), .S1(mutipl_1_s1), .S2(mutipl_1_s2), .S3(mutipl_1_s3),
    .S4(mutipl_1_s4), .S5(mutipl_1_s5));
  ADDSUB addsub_1 (
    .SEL(in_1), .A0(dipswitch_3_p1), .A1(dipswitch_3_p2), .A2(dipswitch_3_p3), .A3(dipswitch_3_p4),
    .B0(dipswitch_4_p1), .B1(dipswitch_4_p2), .B2(dipswitch_4_p3), .B3(dipswitch_4_p4), .S0(addsub_1_s0),
    .S1(addsub_1_s1), .S2(addsub_1_s2), .S3(addsub_1_s3), .S4(addsub_1_s4), .Negative(addsub_1_negative));
  Multiplexer #(.select(2)) multiplexer_1 (
    .in0(combdiv_1_q0), .in1(combdiv_1_r0), .in2(mutipl_1_s0), .in3(addsub_1_s0), .out(multiplexer_1_out),
    .sel(dipswitch_7_sw2));
  Multiplexer #(.select(2)) multiplexer_2 (
    .in0(combdiv_1_q1), .in1(combdiv_1_r1), .in2(mutipl_1_s1), .in3(addsub_1_s1), .out(multiplexer_2_out),
    .sel(dipswitch_7_sw2));
  Multiplexer #(.select(2)) multiplexer_3 (
    .in0(combdiv_1_q2), .in1(combdiv_1_r2), .in2(mutipl_1_s2), .in3(addsub_1_s2), .out(multiplexer_3_out),
    .sel(dipswitch_7_sw2));
  Multiplexer #(.select(2)) multiplexer_4 (
    .in0(combdiv_1_q3), .in1(combdiv_1_r3), .in2(mutipl_1_s3), .in3(addsub_1_s3), .out(multiplexer_4_out),
    .sel(dipswitch_7_sw2));
  Multiplexer #(.select(2)) multiplexer_5 (
    .in0(1'b0), .in1(1'b0), .in2(mutipl_1_s4), .in3(addsub_1_s4), .out(multiplexer_5_out),
    .sel(dipswitch_7_sw2));
  Multiplexer #(.select(2)) multiplexer_6 (
    .in0(1'b0), .in1(1'b0), .in2(mutipl_1_s5), .in3(1'b0), .out(multiplexer_6_out), .sel(dipswitch_7_sw2));
  and and_1 (and_1_out, dipswitch_7_sw2[1], dipswitch_7_sw2[0]);
  and and_2 (and_2_out, and_1_out, addsub_1_negative);
  DipSwitch #(.number(2)) dipswitch_7 (.sw1(dipswitch_7_sw2[1]), .sw2(dipswitch_7_sw2[0]));
  BINTOBCD bintobcd_1 (
    .A(multiplexer_6_out), .B(multiplexer_5_out), .C(multiplexer_4_out), .D(multiplexer_3_out),
    .E(multiplexer_2_out), .F(multiplexer_1_out), .Tens(bintobcd_1_tens), .Ones(bintobcd_1_ones));
  _7_Segment_Display u_7_segment_display_1 (.g(and_2_out));  // open: f, a, b, e, d, c, dp
  _7_Segment_Display u_7_segment_display_2 ();  // open: g, f, a, b, e, d, c, dp
  // BCD_to_7_Segment_decoder bcd_to_7_segment_decoder_1: pin names not known; wires that end beside it: bintobcd_1_tens
  _7_Segment_Display u_7_segment_display_3 ();  // open: g, f, a, b, e, d, c, dp
  // BCD_to_7_Segment_decoder bcd_to_7_segment_decoder_2: pin names not known; wires that end beside it: bintobcd_1_ones
endmodule
